// Logisim project khan.circ as structural Verilog: 3 circuits, main circuit main
module regfile (
  input  Clock,
  input  [1:0] ReadReg1,
  input  [1:0] ReadReg2,
  input  [1:0] WriteReg,
  input  RegWrite,
  input  [15:0] RegDataW,
  output [15:0] RegData1,
  output [15:0] RegData2
);

  wire and_1_out, and_2_out, and_3_out, and_4_out, decoder_1_out0, decoder_1_out1, decoder_1_out2,
       decoder_1_out3;
  wire [15:0] R0_q, R1_q, R2_q, R3_q;

  Decoder #(.select(2)) decoder_1 (
    .out0(decoder_1_out0), .out1(decoder_1_out1), .out2(decoder_1_out2), .out3(decoder_1_out3), .sel(WriteReg));  // open: en
  Register #(.width(16)) R0 (.D(RegDataW), .en(and_1_out), .clk(Clock), .Q(R0_q));  // open: clr
  and and_1 (and_1_out, decoder_1_out0, RegWrite);
  Register #(.width(16)) R1 (.D(RegDataW), .en(and_2_out), .clk(Clock), .Q(R1_q));  // open: clr
  and and_2 (and_2_out, decoder_1_out1, RegWrite);
  Register #(.width(16)) R2 (.D(RegDataW), .en(and_3_out), .clk(Clock), .Q(R2_q));  // open: clr
  and and_3 (and_3_out, decoder_1_out2, RegWrite);
  Register #(.width(16)) R3 (.D(RegDataW), .en(and_4_out), .clk(Clock), .Q(R3_q));  // open: clr
  and and_4 (and_4_out, decoder_1_out3, RegWrite);
  Multiplexer #(.select(2), .width(16)) multiplexer_1 (
    .in0(R0_q), .in1(R1_q), .in2(R2_q), .in3(R3_q), .out(RegData1), .sel(ReadReg1));
  Multiplexer #(.select(2), .width(16)) multiplexer_2 (
    .in0(R0_q), .in1(R1_q), .in2(R2_q), .in3(R3_q), .out(RegData2), .sel(ReadReg2));

  // Notes on the sheet:
  //   RegDataW: pull=down
  //   I pledge my honor that I have abided by the Stevens Honor System.
  //   Joseph DePalo, Rishi Bidarkota
endmodule

module main (
);

  wire clock_1_out;
  wire [1:0] multiplexer_1_out;
  wire [7:0] Instruction_Memory_p2, Instruction_Memory_p3, undriven, undriven_2;
  wire [15:0] adder_1_out, alu_1_aluout, bit_extender_1_out, multiplexer_2_out, multiplexer_3_out, PC_q,
       regfile_1_regdata1, regfile_1_regdata2;

  Clock clock_1 (.out(clock_1_out));
  Adder #(.width(16)) adder_1 (.a(PC_q), .b(16'h2), .out(adder_1_out));  // open: cin, cout
  Register #(.width(16)) PC (.D(adder_1_out), .en(1'b1), .clk(clock_1_out), .Q(PC_q));  // open: clr
  // ROM #(.addrWidth(16), .line("dual")) Instruction_Memory: pin names not known; wires that end beside it: PC_q, Instruction_Memory_p2, Instruction_Memory_p3
  Multiplexer #(.width(2)) multiplexer_1 (
    .in0(Instruction_Memory_p2[2:1]), .in1(Instruction_Memory_p3[1:0]), .out(multiplexer_1_out),
    .sel(Instruction_Memory_p2[6]));
  regfile regfile_1 (
    .Clock(clock_1_out), .ReadReg1(Instruction_Memory_p3[3:2]), .ReadReg2(multiplexer_1_out),
    .WriteReg(Instruction_Memory_p3[1:0]), .RegWrite(Instruction_Memory_p2[7]), .RegDataW(multiplexer_3_out),
    .RegData1(regfile_1_regdata1), .RegData2(regfile_1_regdata2));
  Multiplexer #(.width(16)) multiplexer_2 (
    .in0(regfile_1_regdata2), .in1(bit_extender_1_out), .out(multiplexer_2_out),
    .sel(Instruction_Memory_p2[6]));
  assign bit_extender_1_out = {{9{Instruction_Memory_p2[2]}}, {Instruction_Memory_p2[2:0], Instruction_Memory_p3[7:4]}};  // Bit_Extender bit_extender_1
  alu alu_1 (
    .ALUop(Instruction_Memory_p2[5]), .InputA(regfile_1_regdata1), .InputB(multiplexer_2_out),
    .ALUout(alu_1_aluout));
  // RAM #(.addrWidth(16), .enables("line"), .line("dual")) Data_Memory: pin names not known; wires that end beside it: alu_1_aluout, Instruction_Memory_p2[4], Instruction_Memory_p2[4], Instruction_Memory_p2[4], clock_1_out
  Multiplexer #(.width(16)) multiplexer_3 (
    .in0(alu_1_aluout), .in1({undriven_2, undriven}), .out(multiplexer_3_out), .sel(Instruction_Memory_p2[3]));

  // Notes on the sheet:
  //   contents of Instruction_Memory (hex, n*v repeats v):
  //   c0 70 50 c c1 55 82 2 50 2e e0 aa c8 d c8 2c
  //   Joseph DePalo, Rishi Bidarkota
  //   I pledge my honor that I have abided by the Stevens Honor System.
endmodule

module alu (
  input  ALUop,
  input  [15:0] InputA,
  input  [15:0] InputB,
  output [15:0] ALUout
);

  wire [15:0] adder_1_out, subtractor_1_out;

  Adder #(.width(16)) adder_1 (.a(InputA), .b(InputB), .out(adder_1_out));  // open: cin, cout
  Subtractor #(.width(16)) subtractor_1 (.a(InputA), .b(InputB), .out(subtractor_1_out));  // open: bin, bout
  Multiplexer #(.width(16)) multiplexer_1 (.in0(adder_1_out), .in1(subtractor_1_out), .out(ALUout), .sel(ALUop));
endmodule
